# Fritzing sketch Hardware Sketch (saved by Fritzing 1.0.0d)
breadboards: 1

parts:
  Part1 = Arduino Due (Rev2b)
  Adafruit_MCP9808 = Adafruit MCP9808 [part_number="Adafruit #5027"]
  pH_Circuit1 = pH Circuit
  Conductivity_Circuit1 = Conductivity Circuit
  DS1 = DS18B20 1-Wire Temperature Sensor [part_number=DS18B20]
  R1 = Resistor [tolerance=±20% resistance=4.7k package=THT]
  LED1 = LED - 5mm [color="Red (633nm)" current=0.030A package="5 mm [THT]"]

nets:
  N1: Part1.D16/TX2, Conductivity_Circuit1.RX
  N2: Part1.D17/RX2, Conductivity_Circuit1.TX
  N3: Part1.D18/TX1, pH_Circuit1.RX
  N4: Part1.D19/RX1, pH_Circuit1.TX
  N5: Part1.D20/SDA3, Adafruit_MCP9808.SDA
  N6: Part1.D21/SCL3, Adafruit_MCP9808.SCL
  VCC: Part1.IOREF, Adafruit_MCP9808.VCC, pH_Circuit1.Vcc, Conductivity_Circuit1.Vcc, DS1.VDD, R1.Pin_1
  N7: Part1.D41, DS1.DQ, R1.Pin_0
  GND: Part1.GND, Adafruit_MCP9808.GND, pH_Circuit1.GND, Conductivity_Circuit1.GND, DS1.GND, LED1.anode

notes:
  Sensoren

custom parts:
  Adafruit MCP9808: The MCP9808 digital temperature sensor is one of the more accurate/precise we've ever seen, with a typical accuracy of ±0.25°C over the sensor's -40°C to +125°C range and precision of +0.0625°C. They work great with any microcontroller using standard I2C. With three address jumpers on the back, you can connect up to 8 to a single I2C bus without address collisions. Best of all, a wide voltage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
